# Fritzing sketch MeasuringDistance (saved by Fritzing 0.9.1b)
breadboards: 1

parts:
  Part1 = Arduino Uno (Rev3)
  Part2 = SRF05 Ultrasonic Rangefinder
  R2 = Resistor [tolerance=±1% resistance=470 package=THT]
  R3 = Resistor [tolerance=±1% resistance=470 package=THT]
  R4 = Resistor [tolerance=±1% resistance=470 package=THT]
  LED3 = LED - 3mm [color="Green (555nm)" package="3 mm [THT]"]
  LED4 = LED - 3mm [color="Yellow (592nm)" package="3 mm [THT]"]
  LED5 = LED - 3mm [color="Red (633nm)" package="3 mm [THT]"]

nets:
  N1: Part1.D8, R4.Pin_0
  N2: Part1.D10_PWM/SS, R2.Pin_0
  N3: Part1.D12/MISO, R3.Pin_0
  GND: Part1.GND, Part2.GND, LED3.cathode, LED4.cathode, LED5.cathode
  N4: Part1.D2, Part2.Trig
  N5: Part1.D4, Part2.Echo
  5V: Part1.5V, Part2.VCC
  N6: R2.Pin_1, LED4.anode
  N7: R3.Pin_1, LED3.anode
  N8: R4.Pin_1, LED5.anode
